// Logisim project control_logic.circ as structural Verilog: 11 circuits, main circuit control_logic
module control_logic (
  input  [31:0] inst,
  input  BrEq,
  input  BrLt,
  output PCSel,
  output RegWEn,
  output [2:0] ImmSel,
  output BrUn,
  output ASel,
  output BSel,
  output [3:0] ALUSel,
  output MemRW,
  output [1:0] WBSel,
  output CSRSel,
  output CSRWen
);

  wire nand_1_out;
  wire [1:0] wbselcontrol_1_wbsel;
  wire [2:0] immcontrolver2_1_immsel;
  wire [3:0] aluselcontrol_1_alusel;
  wire [12:0] pcselcontrol_1_pcsel;

  PCSelControl pcselcontrol_1 (
    .Opcode(inst[6:0]), .BrEq(BrLt), .BrLt(BrEq), .Funct3(inst[14:12]), .PCSel(pcselcontrol_1_pcsel[0]));
  RegWEnControl regwencontrol_1 (.Opcode(inst[6:0]), .RegWEn(pcselcontrol_1_pcsel[1]));
  ImmControlVer2 immcontrolver2_1 (.Opcode(inst[6:0]), .ImmSel(immcontrolver2_1_immsel));
  BrUnControl bruncontrol_1 (.Funct3(inst[14:12]), .BrUn(pcselcontrol_1_pcsel[5]));
  ASelControl aselcontrol_1 (.Opcode(inst[6:0]), .ASel(pcselcontrol_1_pcsel[6]));
  BSelControl bselcontrol_1 (.Opcode(inst[6:0]), .BSel(pcselcontrol_1_pcsel[7]));
  ALUSelControl aluselcontrol_1 (
    .Funct7(inst[31:25]), .Funct3(inst[14:12]), .Opcode(inst[6:0]), .ALUSel(aluselcontrol_1_alusel));
  MemRWControl memrwcontrol_1 (.Opcode(inst[6:0]), .MemRW(pcselcontrol_1_pcsel[12]));
  WBSelControl wbselcontrol_1 (.Opcode(inst[6:0]), .WBSel(wbselcontrol_1_wbsel));
  Multiplexer #(.enable("false"), .width(15)) multiplexer_1 (
    .in0({wbselcontrol_1_wbsel, pcselcontrol_1_pcsel[12], aluselcontrol_1_alusel, pcselcontrol_1_pcsel[7:5], immcontrolver2_1_immsel, pcselcontrol_1_pcsel[1:0]}),
    .in1({15{1'b0}}), .out({WBSel, MemRW, ALUSel, BSel, ASel, BrUn, ImmSel, RegWEn, PCSel}), .sel(nand_1_out));
  nand nand_1 (nand_1_out, inst[1], inst[0]);

  // Other names for the same wires on the sheet: opcode[6:0] = inst[6:0]; funct3[2:0] = inst[14:12];
  //   funct7[6:0] = inst[31:25]

  // Notes on the sheet:
  //   INPUTS to your circuit
  //   DON'T CHANGE THE LOCATIONS OF THE INPUTS AND OUTPUTS!
  //   OUTPUT from your circuit
endmodule

module ImmControlVer1 (
  input  [6:0] Opcode,
  output [2:0] ImmControl
);

  wire [2:0] multiplexer_1_out, multiplexer_2_out, multiplexer_3_out, multiplexer_4_out;

  Multiplexer #(.enable("false"), .width(3)) multiplexer_1 (
    .in0(3'b001), .in1(3'b101), .out(multiplexer_1_out), .sel(Opcode[2]));
  Multiplexer #(.enable("false"), .select(2), .width(3)) multiplexer_2 (
    .in0(3'b011), .in1(3'b000), .in2(3'b000), .in3(3'b100), .out(multiplexer_2_out), .sel(Opcode[3:2]));
  Multiplexer #(.enable("false"), .select(2), .width(3)) multiplexer_3 (
    .in0(3'b000), .in1(multiplexer_1_out), .in2(3'b010), .in3(3'b101), .out(multiplexer_3_out),
    .sel(Opcode[5:4]));
  Multiplexer #(.enable("false"), .width(3)) multiplexer_4 (
    .in0(multiplexer_2_out), .in1(3'b000), .out(multiplexer_4_out), .sel(Opcode[4]));
  Multiplexer #(.enable("false"), .width(3)) multiplexer_5 (
    .in0(multiplexer_3_out), .in1(multiplexer_4_out), .out(ImmControl), .sel(Opcode[6]));
endmodule

module ImmControlVer2 (
  input  [6:0] Opcode,
  output [2:0] ImmSel
);

  wire and_1_out, nor_1_out, not_1_out, not_2_out, or_1_out, xor_1_out;

  not not_1 (not_1_out, Opcode[3]);
  nor nor_1 (nor_1_out, Opcode[2], Opcode[3], Opcode[4]);
  xor xor_1 (xor_1_out, Opcode[3], Opcode[4]);
  and and_1 (and_1_out, Opcode[2], not_1_out, Opcode[4]);
  or or_1 (or_1_out, Opcode[2], Opcode[3], Opcode[4]);
  not not_2 (not_2_out, or_1_out);
  and and_2 (ImmSel[1], nor_1_out, Opcode[5]);
  and and_3 (ImmSel[2], Opcode[2], xor_1_out);
  Multiplexer #(.enable("false")) multiplexer_1 (.in0(and_1_out), .in1(not_2_out), .out(ImmSel[0]), .sel(Opcode[6]));

  // Notes on the sheet:
  //   ImmSel bit 0
  //   001 is unimplemented
endmodule

module BSelControl (
  input  [6:0] Opcode,
  output BSel
);

  wire not_1_out, not_2_out, not_3_out;

  not not_1 (not_1_out, Opcode[2]);
  not not_2 (not_2_out, Opcode[3]);
  not not_3 (not_3_out, Opcode[6]);
  nand nand_1 (BSel, not_1_out, not_2_out, Opcode[4], Opcode[5], not_3_out);
endmodule

module ASelControl (
  input  [6:0] Opcode,
  output ASel
);

  wire and_1_out, not_1_out, not_2_out, or_1_out;

  not not_1 (not_1_out, Opcode[2]);
  or or_1 (or_1_out, not_1_out, Opcode[3]);
  not not_2 (not_2_out, Opcode[4]);
  and and_1 (and_1_out, not_2_out, Opcode[5], Opcode[6]);
  and and_2 (ASel, or_1_out, and_1_out);
endmodule

module BrUnControl (
  input  [2:0] Funct3,
  output BrUn
);


  assign BrUn = Funct3[1];
endmodule

module RegWEnControl (
  input  [6:0] Opcode,
  output RegWEn
);

  wire and_1_out, and_2_out, and_3_out, not_1_out, not_2_out, not_3_out, not_4_out;

  not not_1 (not_1_out, Opcode[6]);
  not not_2 (not_2_out, Opcode[6]);
  not not_3 (not_3_out, Opcode[5]);
  not not_4 (not_4_out, Opcode[4]);
  and and_1 (and_1_out, Opcode[2], Opcode[6], Opcode[5], not_4_out);
  and and_2 (and_2_out, not_2_out, not_3_out, not_4_out);
  and and_3 (and_3_out, Opcode[4], not_1_out);
  or or_1 (RegWEn, and_1_out, and_2_out, and_3_out);
endmodule

module PCSelControl (
  input  [6:0] Opcode,
  input  BrEq,
  input  BrLt,
  input  [2:0] Funct3,
  output PCSel
);

  wire and_1_out, and_2_out, multiplexer_1_out, not_1_out, not_2_out, not_3_out, not_4_out, or_1_out,
       or_2_out;

  not not_1 (not_1_out, Opcode[4]);
  not not_2 (not_2_out, Opcode[2]);
  not not_3 (not_3_out, BrEq);
  not not_4 (not_4_out, BrLt);
  and and_1 (and_1_out, not_1_out, Opcode[5], Opcode[6]);
  or or_1 (or_1_out, BrEq, not_4_out);
  and and_2 (and_2_out, not_2_out, multiplexer_1_out);
  Multiplexer #(.enable("false"), .select(2)) multiplexer_1 (
    .in0(BrEq), .in1(not_3_out), .in2(BrLt), .in3(or_1_out), .out(multiplexer_1_out),
    .sel({Funct3[2], Funct3[0]}));
  or or_2 (or_2_out, Opcode[2], and_2_out);
  and and_3 (PCSel, and_1_out, or_2_out);
endmodule

module MemRWControl (
  input  [6:0] Opcode,
  output MemRW
);

  wire not_1_out, not_2_out;

  not not_1 (not_1_out, Opcode[4]);
  and and_1 (MemRW, not_1_out, Opcode[5], not_2_out);
  not not_2 (not_2_out, Opcode[6]);
endmodule

module ALUSelControl (
  input  [6:0] Funct7,
  input  [2:0] Funct3,
  input  [6:0] Opcode,
  output [3:0] ALUSel
);

  wire and_1_out, and_2_out, and_3_out, and_4_out, and_7_out, and_8_out, and_9_out, nor_1_out, not_1_out,
       not_2_out, not_3_out, not_4_out, not_5_out, not_6_out, not_7_out, not_8_out, not_9_out, not_10_out,
       xnor_1_out, xor_1_out;
  wire [2:2] xor_2_out;
  wire [3:0] multiplexer_1_out, multiplexer_2_out, multiplexer_3_out, multiplexer_4_out, multiplexer_5_out,
       multiplexer_6_out, multiplexer_7_out, or_1_out;

  and and_1 (and_1_out, Funct3[2], xnor_1_out);
  xnor xnor_1 (xnor_1_out, Funct3[1], Funct3[0]);
  not not_1 (not_1_out, Funct3[0]);
  and and_2 (and_2_out, not_1_out, Funct3[1], not_2_out);
  not not_2 (not_2_out, Funct3[2]);
  not not_3 (not_3_out, Funct3[1]);
  not not_4 (not_4_out, Funct3[2]);
  not not_5 (not_5_out, Funct3[2]);
  not not_6 (not_6_out, Funct3[2]);
  Multiplexer #(.enable("false"), .width(4)) multiplexer_1 (
    .in0(4'b0000), .in1(4'b1100), .out(multiplexer_1_out), .sel(and_3_out));
  and and_3 (and_3_out, Funct7[5], Opcode[5]);
  or or_1 (or_1_out[0], and_1_out, and_2_out);
  xnor xnor_2 (or_1_out[1], Funct3[0], and_4_out);
  and and_4 (and_4_out, not_3_out, not_4_out);
  xor xor_1 (xor_1_out, Funct3[0], Funct3[1]);
  and and_5 (or_1_out[2], xor_1_out, not_5_out);
  and and_6 (or_1_out[3], Funct3[0], Funct3[1], not_6_out);
  Multiplexer #(.enable("false"), .width(4)) multiplexer_2 (
    .in0(or_1_out), .in1(multiplexer_1_out), .out(multiplexer_2_out), .sel(nor_1_out));
  not not_7 (not_7_out, Funct3[1]);
  nor nor_1 (nor_1_out, Funct3[0], Funct3[1], Funct3[2]);
  xor xor_2 (xor_2_out[2], Funct3[0], Funct3[1]);
  and and_7 (and_7_out, Opcode[4], not_8_out);
  not not_8 (not_8_out, Opcode[6]);
  not not_9 (not_9_out, Opcode[3]);
  and and_8 (and_8_out, Opcode[2], not_9_out, Opcode[4], not_10_out);
  not not_10 (not_10_out, Opcode[6]);
  Multiplexer #(.enable("false"), .width(4)) multiplexer_3 (
    .in0(multiplexer_2_out), .in1(multiplexer_4_out), .out(multiplexer_3_out), .sel(and_9_out));
  Multiplexer #(.enable("false"), .width(4)) multiplexer_4 (
    .in0(4'b0100), .in1(4'b0101), .out(multiplexer_4_out), .sel(Funct7[5]));
  and and_9 (and_9_out, Funct3[0], not_7_out, Funct3[2]);
  Multiplexer #(.enable("false"), .width(4)) multiplexer_5 (
    .in0(multiplexer_3_out), .in1({1'b1, xor_2_out[2], 1'b1, Funct3[1]}), .out(multiplexer_5_out),
    .sel(Funct7[0]));
  Multiplexer #(.enable("false"), .width(4)) multiplexer_6 (
    .in0(4'b0000), .in1(multiplexer_5_out), .out(multiplexer_6_out), .sel(and_7_out));
  Multiplexer #(.enable("false"), .width(4)) multiplexer_7 (
    .in0(4'b0000), .in1(4'b1101), .out(multiplexer_7_out), .sel(Opcode[5]));
  Multiplexer #(.enable("false"), .width(4)) multiplexer_8 (
    .in0(multiplexer_6_out), .in1(multiplexer_7_out), .out(ALUSel), .sel(and_8_out));

  // Notes on the sheet:
  //   and / sub
  //   add / other
  //   sra / srl
  //   M-Type
  //   Other operations for R, I Type
  //   shift right / (add / other)
  //   M-Type or R/I
  //   Depends or Add
  //   bsel for J-Type
endmodule

module WBSelControl (
  input  [6:0] Opcode,
  output [1:0] WBSel
);

  wire and_1_out, nor_1_out, not_1_out;
  wire [1:0] multiplexer_1_out;

  nor nor_1 (nor_1_out, Opcode[4], Opcode[5], Opcode[6]);
  and and_1 (and_1_out, Opcode[6], Opcode[5], not_1_out);
  not not_1 (not_1_out, Opcode[4]);
  Multiplexer #(.enable("false"), .width(2)) multiplexer_1 (
    .in0(2'b00), .in1(2'b01), .out(multiplexer_1_out), .sel(nor_1_out));
  Multiplexer #(.enable("false"), .width(2)) multiplexer_2 (
    .in0(multiplexer_1_out), .in1(2'b10), .out(WBSel), .sel(and_1_out));
endmodule
