// Logisim project cpu.circ as structural Verilog: 2 circuits, main circuit cpu
module cpu (
  input  clk,
  input  [31:0] INSTRUCTION,
  input  [31:0] READ_DATA,
  input  rst,
  output [31:0] WRITE_ADDRESS,
  output [31:0] PROGRAM_COUNTER,
  output [31:0] ra,
  output [31:0] sp,
  output [31:0] t0,
  output [31:0] t1,
  output [31:0] t2,
  output [31:0] s0,
  output [31:0] s1,
  output [31:0] a0,
  output [31:0] tohost,
  output [3:0] WRITE_ENABLE,
  output [31:0] WRITE_DATA
);

  wire branch_comp_1_breq, branch_comp_1_brlt, Control_brun;
  wire [1:0] Control_wbsel;
  wire [2:0] Control_immsel;
  wire [3:0] bit_extender_1_out, Control_alusel, Control_WB_q;
  wire [4:0] Control_ME_q;
  wire [8:0] Control_pcsel;
  wire [10:0] Control_EX_q;
  wire [31:0] adder_1_out, adder_2_out, alu_1_result, alu_forwarding_1_data_out_1,
       alu_forwarding_1_data_out_2, alu_WB_q, imm_EX_q, imm_gen_1_imm, inst_EX_q, inst_ID_q, inst_ME_q,
       inst_WB_q, mem_WB_q, multiplexer_1_out, multiplexer_2_out, multiplexer_3_out, multiplexer_4_out,
       PC_EX_q, PC_ID_q, PC_ME_q, PCplus4_WB_q, ra1_EX_q, ra2_EX_q, regfile_1_read_data_1,
       regfile_1_read_data_2;

  Adder #(.width(32)) adder_1 (.a(PROGRAM_COUNTER), .b(32'h4), .out(adder_1_out));  // open: cin, cout
  Register #(.width(32)) PC (.D(multiplexer_1_out), .en(1'b1), .clk(clk), .Q(PROGRAM_COUNTER), .clr(rst));
  Multiplexer #(.enable("false"), .width(32)) multiplexer_1 (
    .in0(adder_1_out), .in1(multiplexer_4_out), .out(multiplexer_1_out), .sel(Control_WB_q[0]));
  Register #(.width(32)) PC_ID (.D(PROGRAM_COUNTER), .en(1'b1), .clk(clk), .Q(PC_ID_q), .clr(rst));
  Register #(.width(32)) inst_ID (.D(INSTRUCTION), .en(1'b1), .clk(clk), .Q(inst_ID_q), .clr(rst));
  control_logic Control (
    .PCSel(Control_pcsel[0]), .RegWEn(Control_pcsel[1]), .ImmSel(Control_immsel), .BrUn(Control_brun),
    .ASel(Control_pcsel[2]), .BSel(Control_pcsel[3]), .ALUSel(Control_alusel), .MemRW(Control_pcsel[8]),
    .WBSel(Control_wbsel), .inst(inst_ID_q), .BrEq(branch_comp_1_breq), .BrLt(branch_comp_1_brlt));  // open: CSRWen, CSRSel
  regfile regfile_1 (
    .rs1(inst_ID_q[19:15]), .rs2(inst_ID_q[24:20]), .rd(inst_WB_q[11:7]), .Write_Data(multiplexer_4_out),
    .RegWEn(Control_WB_q[1]), .clk(clk), .ra(ra), .sp(sp), .t0(t0), .t1(t1), .t2(t2), .s0(s0), .s1(s1),
    .a0(a0), .Read_Data_1(regfile_1_read_data_1), .Read_Data_2(regfile_1_read_data_2));
  imm_gen imm_gen_1 (.inst(inst_ID_q), .ImmSel(Control_immsel), .imm(imm_gen_1_imm));
  branch_comp branch_comp_1 (
    .rs1(regfile_1_read_data_1), .rs2(regfile_1_read_data_2), .BrUn(Control_brun), .BrEq(branch_comp_1_breq),
    .BrLt(branch_comp_1_brlt));
  Register #(.width(32)) PC_EX (.D(PC_ID_q), .en(1'b1), .clk(clk), .Q(PC_EX_q), .clr(rst));
  Register #(.width(32)) ra1_EX (.D(regfile_1_read_data_1), .en(1'b1), .clk(clk), .Q(ra1_EX_q), .clr(rst));
  Register #(.width(32)) ra2_EX (.D(regfile_1_read_data_2), .en(1'b1), .clk(clk), .Q(ra2_EX_q), .clr(rst));
  Register #(.width(32)) imm_EX (.D(imm_gen_1_imm), .en(1'b1), .clk(clk), .Q(imm_EX_q), .clr(rst));
  Register #(.width(32)) inst_EX (.D(inst_ID_q), .en(1'b1), .clk(clk), .Q(inst_EX_q), .clr(rst));
  Register #(.width(11)) Control_EX (
    .D({Control_wbsel, Control_pcsel[8], Control_alusel, Control_pcsel[3:0]}), .clk(clk), .Q(Control_EX_q),
    .clr(rst));  // open: en
  ALU_Forwarding alu_forwarding_1 (
    .ALU_Result(WRITE_ADDRESS), .Read_Data_1(ra1_EX_q), .Read_Data_2(ra2_EX_q), .inst_EX(inst_EX_q),
    .inst_ME(inst_ME_q), .Data_Out_1(alu_forwarding_1_data_out_1), .Data_Out_2(alu_forwarding_1_data_out_2));
  Multiplexer #(.enable("false"), .width(32)) multiplexer_2 (
    .in0(alu_forwarding_1_data_out_1), .in1(PC_EX_q), .out(multiplexer_2_out), .sel(Control_EX_q[2]));
  Multiplexer #(.enable("false"), .width(32)) multiplexer_3 (
    .in0(alu_forwarding_1_data_out_2), .in1(imm_EX_q), .out(multiplexer_3_out), .sel(Control_EX_q[3]));
  // csr csr_1: pin names not known; wires that end beside it: clk, tohost
  Register #(.width(32)) PC_ME (.D(PC_EX_q), .en(1'b1), .clk(clk), .Q(PC_ME_q), .clr(rst));
  Register #(.width(32)) alu_ME (.D(alu_1_result), .en(1'b1), .clk(clk), .Q(WRITE_ADDRESS), .clr(rst));
  alu alu_1 (.Result(alu_1_result), .A(multiplexer_2_out), .B(multiplexer_3_out), .ALUSel(Control_EX_q[7:4]));
  Register #(.width(32)) ra2_ME (.D(alu_forwarding_1_data_out_2), .en(1'b1), .clk(clk), .Q(WRITE_DATA), .clr(rst));
  Register #(.width(32)) inst_ME (.D(inst_EX_q), .en(1'b1), .clk(clk), .Q(inst_ME_q), .clr(rst));
  Register #(.width(5)) Control_ME (
    .D({Control_EX_q[10:8], Control_EX_q[1:0]}), .en(1'b1), .clk(clk), .Q(Control_ME_q), .clr(rst));
  assign bit_extender_1_out = {{3{1'b0}}, Control_ME_q[2]};  // Bit_Extender bit_extender_1
  Shifter #(.width(4)) shifter_1 (.in(bit_extender_1_out), .\dist (inst_ME_q[13:12]), .out(WRITE_ENABLE));
  Adder #(.width(32)) adder_2 (.a(PC_ME_q), .b(32'h4), .out(adder_2_out));  // open: cin, cout
  Register #(.width(32)) PCplus4_WB (.D(adder_2_out), .en(1'b1), .clk(clk), .Q(PCplus4_WB_q), .clr(rst));
  Register #(.width(32)) mem_WB (.D(READ_DATA), .en(1'b1), .clk(clk), .Q(mem_WB_q), .clr(rst));
  Register #(.width(32)) alu_WB (.D(WRITE_ADDRESS), .en(1'b1), .clk(clk), .Q(alu_WB_q), .clr(rst));
  Register #(.width(32)) inst_WB (.D(inst_ME_q), .en(1'b1), .clk(clk), .Q(inst_WB_q), .clr(rst));
  Register #(.width(4)) Control_WB (
    .D({Control_ME_q[4:3], Control_ME_q[1:0]}), .en(1'b1), .clk(clk), .Q(Control_WB_q), .clr(rst));
  Multiplexer #(.enable("false"), .select(2), .width(32)) multiplexer_4 (
    .in0(alu_WB_q), .in1(mem_WB_q), .in2(PCplus4_WB_q), .out(multiplexer_4_out), .sel(Control_WB_q[3:2]));  // open: in3

  // Notes on the sheet:
  //   Output to IMEM
  //   IMEM (do **NOT** move this)
  //   Inputs from IMEM
  //   Inputs/Outputs for testing. Do **NOT** move these.
  //   Outputs To DMEM
  //   DMEM (do **NOT** move this)
  //   Inputs From DMEM
endmodule

module ALU_Forwarding (
  input  [31:0] ALU_Result,
  input  [31:0] Read_Data_1,
  input  [31:0] Read_Data_2,
  input  [31:0] inst_EX,
  input  [31:0] inst_ME,
  output [31:0] Data_Out_1,
  output [31:0] Data_Out_2
);

  wire and_1_out, and_2_out, and_3_out, and_4_out, and_5_out, and_6_out, and_7_out, multiplexer_3_out,
       nand_1_out, nor_1_out, not_1_out, not_2_out, not_3_out, not_4_out, not_5_out, or_1_out;
  wire [4:0] xnor_1_out, xnor_2_out;

  assign xnor_1_out = ~(inst_EX[19:15] ^ inst_ME[11:7]);  // XNOR_Gate xnor_1, 5 bits wide
  assign xnor_2_out = ~(inst_EX[24:20] ^ inst_ME[11:7]);  // XNOR_Gate xnor_2, 5 bits wide
  and and_1 (and_1_out, xnor_1_out[0], xnor_1_out[1], xnor_1_out[2], xnor_1_out[3], xnor_1_out[4]);
  and and_2 (and_2_out, xnor_2_out[0], xnor_2_out[1], xnor_2_out[2], xnor_2_out[3], xnor_2_out[4]);
  not not_1 (not_1_out, inst_EX[3]);
  not not_2 (not_2_out, inst_EX[2]);
  nand nand_1 (nand_1_out, inst_EX[6], inst_EX[4]);
  and and_3 (and_3_out, nand_1_out, inst_EX[5], not_1_out, not_2_out);
  Multiplexer #(.enable("false"), .width(32)) multiplexer_1 (
    .in0(Read_Data_1), .in1(ALU_Result), .out(Data_Out_1), .sel(and_4_out));
  and and_4 (and_4_out, and_1_out, multiplexer_3_out, and_7_out);
  Multiplexer #(.enable("false"), .width(32)) multiplexer_2 (
    .in0(Read_Data_2), .in1(ALU_Result), .out(Data_Out_2), .sel(and_5_out));
  and and_5 (and_5_out, and_2_out, and_3_out, and_7_out);
  and and_6 (and_6_out, inst_EX[6], inst_EX[5]);
  not not_3 (not_3_out, inst_EX[2]);
  Multiplexer #(.enable("false")) multiplexer_3 (
    .in0(not_3_out), .in1(nor_1_out), .out(multiplexer_3_out), .sel(and_6_out));
  nor nor_1 (nor_1_out, inst_EX[4], inst_EX[3]);
  not not_4 (not_4_out, inst_ME[5]);
  not not_5 (not_5_out, inst_ME[6]);
  or or_1 (or_1_out, not_4_out, inst_ME[4]);
  and and_7 (and_7_out, not_5_out, or_1_out);

  // Other names for the same wires on the sheet: opcode_EX[6:0] = inst_EX[6:0]; opcode_ME[6:0] = inst_ME[6:0]

  // Notes on the sheet:
  //   We first treat 110XX11 as no data hazard
  //   determine the instruction type
  //   Check whether rs1_EX == rd_ME or rs2_EX == rd_ME
  //   R, S, B have rs2
  //   rs1
  //   if 11XXX, XX00X, else XXXX0
  //   R, I, U have rd
endmodule
