// Logisim project imm_gen.circ as structural Verilog: 1 circuit, main circuit imm_gen
module imm_gen (
  input  [31:0] inst,
  input  [2:0] ImmSel,
  output [31:0] imm
);

  wire [31:0] bit_extender_1_out, bit_extender_2_out, bit_extender_3_out, bit_extender_4_out,
       bit_extender_5_out, multiplexer_1_out, multiplexer_2_out, multiplexer_3_out, multiplexer_4_out,
       shifter_1_out, shifter_2_out, shifter_3_out;

  assign bit_extender_1_out = {{12{inst[31]}}, inst[31:12]};  // Bit_Extender bit_extender_1
  assign bit_extender_2_out = {{20{inst[31]}}, inst[31:20]};  // Bit_Extender bit_extender_2
  assign bit_extender_3_out = {{20{inst[31]}}, {inst[31:25], inst[11:7]}};  // Bit_Extender bit_extender_3
  assign bit_extender_4_out = {{21{inst[31]}}, {inst[31:25], inst[11:8]}};  // Bit_Extender bit_extender_4
  assign bit_extender_5_out = {{13{inst[31]}}, {inst[31], inst[19:12], inst[30:21]}};  // Bit_Extender bit_extender_5
  Shifter #(.width(32)) shifter_1 (.in(bit_extender_4_out), .\dist (5'b00001), .out(shifter_1_out));
  Shifter #(.width(32)) shifter_2 (.in(bit_extender_5_out), .\dist (5'b00001), .out(shifter_2_out));
  Shifter #(.width(32)) shifter_3 (.in(bit_extender_1_out), .\dist (5'b01100), .out(shifter_3_out));
  Multiplexer #(.enable("false"), .width(32)) multiplexer_1 (
    .in0(shifter_1_out), .in1(bit_extender_4_out), .out(multiplexer_1_out), .sel(inst[7]));
  Multiplexer #(.enable("false"), .width(32)) multiplexer_2 (
    .in0(shifter_2_out), .in1(bit_extender_5_out), .out(multiplexer_2_out), .sel(inst[20]));
  Multiplexer #(.enable("false"), .width(32)) multiplexer_3 (
    .in0(bit_extender_3_out), .in1(multiplexer_1_out), .out(multiplexer_3_out), .sel(ImmSel[0]));
  Multiplexer #(.enable("false"), .width(32)) multiplexer_4 (
    .in0(multiplexer_2_out), .in1(shifter_3_out), .out(multiplexer_4_out), .sel(ImmSel[0]));
  Multiplexer #(.enable("false"), .select(2), .width(32)) multiplexer_5 (
    .in0(bit_extender_2_out), .in1(multiplexer_3_out), .in2(multiplexer_4_out), .in3({32{1'b0}}), .out(imm),
    .sel(ImmSel[2:1]));

  // Notes on the sheet:
  //   INPUTS to your circuit
  //   I-Type: 000, 001
  //   S-Type: 010
  //   B-Type: 011
  //   J-Type: 100
  //   U-Type: 101
  //   001 is unimplemented
  //   DON'T CHANGE THE LOCATIONS OF THE INPUTS AND OUTPUTS!
  //   OUTPUT from your circuit
endmodule
