// Logisim project regfile.circ as structural Verilog: 1 circuit, main circuit regfile
module regfile (
  input  [4:0] rs1,
  input  [4:0] rs2,
  input  [4:0] rd,
  input  [31:0] Write_Data,
  input  RegWEn,
  input  clk,
  output [31:0] ra,
  output [31:0] sp,
  output [31:0] t0,
  output [31:0] t1,
  output [31:0] t2,
  output [31:0] s0,
  output [31:0] s1,
  output [31:0] a0,
  output [31:0] Read_Data_1,
  output [31:0] Read_Data_2
);

  wire demultiplexer_1_out0, demultiplexer_1_out1, demultiplexer_1_out2, demultiplexer_1_out3,
       demultiplexer_2_out1, demultiplexer_2_out2, demultiplexer_2_out3, demultiplexer_2_out4,
       demultiplexer_2_out5, demultiplexer_2_out6, demultiplexer_2_out7, demultiplexer_3_out0,
       demultiplexer_3_out1, demultiplexer_3_out2, demultiplexer_3_out3, demultiplexer_3_out4,
       demultiplexer_3_out5, demultiplexer_3_out6, demultiplexer_3_out7, demultiplexer_4_out0,
       demultiplexer_4_out1, demultiplexer_4_out2, demultiplexer_4_out3, demultiplexer_4_out4,
       demultiplexer_4_out5, demultiplexer_4_out6, demultiplexer_4_out7, demultiplexer_5_out0,
       demultiplexer_5_out1, demultiplexer_5_out2, demultiplexer_5_out3, demultiplexer_5_out4,
       demultiplexer_5_out5, demultiplexer_5_out6, demultiplexer_5_out7;
  wire [31:0] multiplexer_1_out, multiplexer_2_out, multiplexer_3_out, multiplexer_4_out, multiplexer_5_out,
       multiplexer_6_out, multiplexer_7_out, multiplexer_8_out, register_1_q, register_2_q, register_3_q,
       register_4_q, register_5_q, register_6_q, register_7_q, register_8_q, register_9_q, register_10_q,
       register_11_q, register_12_q, register_13_q, register_14_q, register_15_q, register_16_q, x0_q, x3_q,
       x4_q, x11_q, x12_q, x13_q, x14_q, x15_q;

  Demultiplexer #(.enable("false"), .select(2)) demultiplexer_1 (
    .out0(demultiplexer_1_out0), .out1(demultiplexer_1_out1), .out2(demultiplexer_1_out2),
    .out3(demultiplexer_1_out3), .in(RegWEn), .sel(rd[4:3]));
  Demultiplexer #(.enable("false"), .select(3)) demultiplexer_2 (
    .out1(demultiplexer_2_out1), .out2(demultiplexer_2_out2), .out3(demultiplexer_2_out3),
    .out4(demultiplexer_2_out4), .out5(demultiplexer_2_out5), .out6(demultiplexer_2_out6),
    .out7(demultiplexer_2_out7), .in(demultiplexer_1_out0), .sel(rd[2:0]));  // open: out0
  Demultiplexer #(.enable("false"), .select(3)) demultiplexer_3 (
    .out0(demultiplexer_3_out0), .out1(demultiplexer_3_out1), .out2(demultiplexer_3_out2),
    .out3(demultiplexer_3_out3), .out4(demultiplexer_3_out4), .out5(demultiplexer_3_out5),
    .out6(demultiplexer_3_out6), .out7(demultiplexer_3_out7), .in(demultiplexer_1_out1), .sel(rd[2:0]));
  Demultiplexer #(.enable("false"), .select(3)) demultiplexer_4 (
    .out0(demultiplexer_4_out0), .out1(demultiplexer_4_out1), .out2(demultiplexer_4_out2),
    .out3(demultiplexer_4_out3), .out4(demultiplexer_4_out4), .out5(demultiplexer_4_out5),
    .out6(demultiplexer_4_out6), .out7(demultiplexer_4_out7), .in(demultiplexer_1_out2), .sel(rd[2:0]));
  Demultiplexer #(.enable("false"), .select(3)) demultiplexer_5 (
    .out0(demultiplexer_5_out0), .out1(demultiplexer_5_out1), .out2(demultiplexer_5_out2),
    .out3(demultiplexer_5_out3), .out4(demultiplexer_5_out4), .out5(demultiplexer_5_out5),
    .out6(demultiplexer_5_out6), .out7(demultiplexer_5_out7), .in(demultiplexer_1_out3), .sel(rd[2:0]));
  Register #(.width(32)) x0 (.D({32{1'b0}}), .en(1'b0), .clk(clk), .Q(x0_q));  // open: clr
  Register #(.width(32)) x8 (.D(Write_Data), .en(demultiplexer_3_out0), .clk(clk), .Q(s0));  // open: clr
  Register #(.width(32)) register_1 (
    .D(Write_Data), .en(demultiplexer_4_out0), .clk(clk), .Q(register_1_q));  // open: clr
  Register #(.width(32)) register_2 (
    .D(Write_Data), .en(demultiplexer_5_out0), .clk(clk), .Q(register_2_q));  // open: clr
  Register #(.width(32)) x1 (.D(Write_Data), .en(demultiplexer_2_out1), .clk(clk), .Q(ra));  // open: clr
  Register #(.width(32)) x9 (.D(Write_Data), .en(demultiplexer_3_out1), .clk(clk), .Q(s1));  // open: clr
  Register #(.width(32)) register_3 (
    .D(Write_Data), .en(demultiplexer_4_out1), .clk(clk), .Q(register_3_q));  // open: clr
  Register #(.width(32)) register_4 (
    .D(Write_Data), .en(demultiplexer_5_out1), .clk(clk), .Q(register_4_q));  // open: clr
  Register #(.width(32)) x2 (.D(Write_Data), .en(demultiplexer_2_out2), .clk(clk), .Q(sp));  // open: clr
  Register #(.width(32)) x10 (.D(Write_Data), .en(demultiplexer_3_out2), .clk(clk), .Q(a0));  // open: clr
  Register #(.width(32)) register_5 (
    .D(Write_Data), .en(demultiplexer_4_out2), .clk(clk), .Q(register_5_q));  // open: clr
  Register #(.width(32)) register_6 (
    .D(Write_Data), .en(demultiplexer_5_out2), .clk(clk), .Q(register_6_q));  // open: clr
  Register #(.width(32)) x3 (.D(Write_Data), .en(demultiplexer_2_out3), .clk(clk), .Q(x3_q));  // open: clr
  Register #(.width(32)) x11 (.D(Write_Data), .en(demultiplexer_3_out3), .clk(clk), .Q(x11_q));  // open: clr
  Register #(.width(32)) register_7 (
    .D(Write_Data), .en(demultiplexer_4_out3), .clk(clk), .Q(register_7_q));  // open: clr
  Register #(.width(32)) register_8 (
    .D(Write_Data), .en(demultiplexer_5_out3), .clk(clk), .Q(register_8_q));  // open: clr
  Register #(.width(32)) x4 (.D(Write_Data), .en(demultiplexer_2_out4), .clk(clk), .Q(x4_q));  // open: clr
  Register #(.width(32)) x12 (.D(Write_Data), .en(demultiplexer_3_out4), .clk(clk), .Q(x12_q));  // open: clr
  Register #(.width(32)) register_9 (
    .D(Write_Data), .en(demultiplexer_4_out4), .clk(clk), .Q(register_9_q));  // open: clr
  Register #(.width(32)) register_10 (
    .D(Write_Data), .en(demultiplexer_5_out4), .clk(clk), .Q(register_10_q));  // open: clr
  Register #(.width(32)) x5 (.D(Write_Data), .en(demultiplexer_2_out5), .clk(clk), .Q(t0));  // open: clr
  Register #(.width(32)) x13 (.D(Write_Data), .en(demultiplexer_3_out5), .clk(clk), .Q(x13_q));  // open: clr
  Register #(.width(32)) register_11 (
    .D(Write_Data), .en(demultiplexer_4_out5), .clk(clk), .Q(register_11_q));  // open: clr
  Register #(.width(32)) register_12 (
    .D(Write_Data), .en(demultiplexer_5_out5), .clk(clk), .Q(register_12_q));  // open: clr
  Register #(.width(32)) x6 (.D(Write_Data), .en(demultiplexer_2_out6), .clk(clk), .Q(t1));  // open: clr
  Register #(.width(32)) x14 (.D(Write_Data), .en(demultiplexer_3_out6), .clk(clk), .Q(x14_q));  // open: clr
  Register #(.width(32)) register_13 (
    .D(Write_Data), .en(demultiplexer_4_out6), .clk(clk), .Q(register_13_q));  // open: clr
  Register #(.width(32)) register_14 (
    .D(Write_Data), .en(demultiplexer_5_out6), .clk(clk), .Q(register_14_q));  // open: clr
  Register #(.width(32)) x7 (.D(Write_Data), .en(demultiplexer_2_out7), .clk(clk), .Q(t2));  // open: clr
  Register #(.width(32)) x15 (.D(Write_Data), .en(demultiplexer_3_out7), .clk(clk), .Q(x15_q));  // open: clr
  Register #(.width(32)) register_15 (
    .D(Write_Data), .en(demultiplexer_4_out7), .clk(clk), .Q(register_15_q));  // open: clr
  Register #(.width(32)) register_16 (
    .D(Write_Data), .en(demultiplexer_5_out7), .clk(clk), .Q(register_16_q));  // open: clr
  Multiplexer #(.enable("false"), .select(3), .width(32)) multiplexer_1 (
    .in0(x0_q), .in1(ra), .in2(sp), .in3(x3_q), .in4(x4_q), .in5(t0), .in6(t1), .in7(t2),
    .out(multiplexer_1_out), .sel(rs1[2:0]));
  Multiplexer #(.enable("false"), .select(3), .width(32)) multiplexer_2 (
    .in0(x0_q), .in1(ra), .in2(sp), .in3(x3_q), .in4(x4_q), .in5(t0), .in6(t1), .in7(t2),
    .out(multiplexer_2_out), .sel(rs2[2:0]));
  Multiplexer #(.enable("false"), .select(3), .width(32)) multiplexer_3 (
    .in0(s0), .in1(s1), .in2(a0), .in3(x11_q), .in4(x12_q), .in5(x13_q), .in6(x14_q), .in7(x15_q),
    .out(multiplexer_3_out), .sel(rs1[2:0]));
  Multiplexer #(.enable("false"), .select(3), .width(32)) multiplexer_4 (
    .in0(s0), .in1(s1), .in2(a0), .in3(x11_q), .in4(x12_q), .in5(x13_q), .in6(x14_q), .in7(x15_q),
    .out(multiplexer_4_out), .sel(rs2[2:0]));
  Multiplexer #(.enable("false"), .select(3), .width(32)) multiplexer_5 (
    .in0(register_1_q), .in1(register_3_q), .in2(register_5_q), .in3(register_7_q), .in4(register_9_q),
    .in5(register_11_q), .in6(register_13_q), .in7(register_15_q), .out(multiplexer_5_out), .sel(rs1[2:0]));
  Multiplexer #(.enable("false"), .select(3), .width(32)) multiplexer_6 (
    .in0(register_1_q), .in1(register_3_q), .in2(register_5_q), .in3(register_7_q), .in4(register_9_q),
    .in5(register_11_q), .in6(register_13_q), .in7(register_15_q), .out(multiplexer_6_out), .sel(rs2[2:0]));
  Multiplexer #(.enable("false"), .select(3), .width(32)) multiplexer_7 (
    .in0(register_2_q), .in1(register_4_q), .in2(register_6_q), .in3(register_8_q), .in4(register_10_q),
    .in5(register_12_q), .in6(register_14_q), .in7(register_16_q), .out(multiplexer_7_out), .sel(rs1[2:0]));
  Multiplexer #(.enable("false"), .select(3), .width(32)) multiplexer_8 (
    .in0(register_2_q), .in1(register_4_q), .in2(register_6_q), .in3(register_8_q), .in4(register_10_q),
    .in5(register_12_q), .in6(register_14_q), .in7(register_16_q), .out(multiplexer_8_out), .sel(rs2[2:0]));
  Multiplexer #(.enable("false"), .select(2), .width(32)) multiplexer_9 (
    .in0(multiplexer_1_out), .in1(multiplexer_3_out), .in2(multiplexer_5_out), .in3(multiplexer_7_out),
    .out(Read_Data_1), .sel(rs1[4:3]));
  Multiplexer #(.enable("false"), .select(2), .width(32)) multiplexer_10 (
    .in0(multiplexer_2_out), .in1(multiplexer_4_out), .in2(multiplexer_6_out), .in3(multiplexer_8_out),
    .out(Read_Data_2), .sel(rs2[4:3]));

  // Other names for the same wires on the sheet: read_data1[31:0] = Read_Data_1; read_data2[31:0] = Read_Data_2;
  //   read_reg1[4:0] = rs1; read_reg2[4:0] = rs2; write_en = RegWEn; write_reg[4:0] = rd

  // Notes on the sheet:
  //   INPUTS to your circuit
  //   DON'T CHANGE THE LOCATIONS OF THE INPUTS AND OUTPUTS!
  //   These are DEBUG/TEST outputs from your circuit.
  //   OUTPUTS from your circuit
endmodule
